# Fritzing sketch Afficheur lcd + arduino due (platine) (saved by Fritzing 0.9.3b)
breadboards: 1

parts:
  Composant1 = Arduino Due (Rev2b)
  LCD1 = LCD screen
  R1 = Trimmer Potentiometer [maximum_resistance=10kΩ package=THT]

nets:
  N1: Composant1.D11_PWM, LCD1.E
  N2: Composant1.D12_PWM, LCD1.RS
  N3: Composant1.D2_PWM, LCD1.DB7
  N4: Composant1.D3_PWM, LCD1.DB6
  N5: Composant1.D4_PWM/SS1, LCD1.DB5
  N6: Composant1.D5_PWM, LCD1.DB4
  N7: LCD1.VSS, LCD1.R/W, LCD1.LED-, R1.leg2
  N8: LCD1.VDD, R1.leg1
  N9: LCD1.V0, R1.wiper
